// Logisim project control_logic_unit.circ as structural Verilog: 3 circuits, main circuit main
module main (
  input  in_1,
  input  in_2,
  input  in_3,
  input  in_4,
  input  in_5
);

  wire CLOCK0, fetch_clock, fetch_cycle, high_cycle, INT_MASK_FLAG, INT_REQUEST, inv_CLOCK, low_cycle, RESET,
       reset_high_cycle, reset_low_cycle, reset_sync;
  wire [7:0] DATA, INS;
  wire [9:0] select_opcode;

  Hex_Digit_Display hex_digit_display_1 (.value(INS[7:4]));  // open: dp
  Hex_Digit_Display hex_digit_display_2 (.value(INS[3:0]));  // open: dp
  not not_1 (inv_CLOCK, CLOCK0);
  LED led_1 (.in(fetch_cycle));
  LED led_2 (.in(low_cycle));
  LED led_3 (.in(high_cycle));
  sequenciador sequenciador_1 (
    .RESET(RESET), .inv_CLOCK(inv_CLOCK), .inv_UC_restart_cycle(in_1), .inv_UC_halt(in_2),
    .reset_sync(reset_sync), .reset_low_cycle(reset_low_cycle), .reset_high_cycle(reset_high_cycle),
    .fetch_cycle(fetch_cycle), .low_cycle(low_cycle), .high_cycle(high_cycle));
  Button button_1 (.out(RESET));
  Clock clock_1 (.out(CLOCK0));
  decodificador decodificador_1 (
    .inv_UC_clear_interrupt_mask(in_3), .INT_REQUEST(INT_REQUEST), .inv_UC_set_interrupt_mask(in_4),
    .DATA(DATA), .reset_sync(reset_sync), .inv_UC_restart_cycle(in_1), .reset_low_cycle(reset_low_cycle),
    .reset_high_cycle(reset_high_cycle), .inv_UC_int_ready(in_5), .fetch_clock(fetch_clock),
    .fetch_cycle(fetch_cycle), .low_cycle(low_cycle), .high_cycle(high_cycle), .select_opcode(select_opcode),
    .INS(INS), .INT_MASK_FLAG(INT_MASK_FLAG));

  // Other names for the same wires on the sheet: inv_UC_clear_interrupt_mask = in_3; inv_UC_halt = in_2;
  //   inv_UC_int_ready = in_5; inv_UC_restart_cycle = in_1; inv_UC_set_interrupt_mask = in_4
endmodule

module sequenciador (
  input  RESET,
  input  inv_CLOCK,
  input  inv_UC_restart_cycle,
  input  inv_UC_halt,
  output reset_sync,
  output reset_low_cycle,
  output reset_high_cycle,
  output fetch_cycle,
  output low_cycle,
  output high_cycle
);

  wire inv_restart_cycle, n74138_1_pin4, n74138_1_pin10, n74138_1_pin11, n74138_1_pin12, n74138_1_pin13,
       n74138_1_pin14, n74138_1_pin15, n74193_1_pin1, n74193_1_pin4, n74193_1_pin10, n74193_1_pin11,
       n74193_1_pin15, QA, QB, QC;

  _74193 u_74193_1 (
    .pin1(n74193_1_pin1), .pin2(QB), .pin3(QA), .pin4(n74193_1_pin4), .pin5(inv_CLOCK), .pin6(QC),
    .pin15(n74193_1_pin15), .pin14(RESET), .pin11(n74193_1_pin11), .pin10(n74193_1_pin10),
    .pin9(n74193_1_pin10));  // open: pin7, pin13, pin12
  and and_1 (n74193_1_pin11, inv_restart_cycle, inv_UC_restart_cycle);
  _74138 u_74138_1 (
    .pin1(QA), .pin2(QB), .pin3(QC), .pin4(n74138_1_pin4), .pin5(n74138_1_pin4), .pin6(inv_UC_halt),
    .pin15(n74138_1_pin15), .pin14(n74138_1_pin14), .pin13(n74138_1_pin13), .pin12(n74138_1_pin12),
    .pin11(n74138_1_pin11), .pin10(n74138_1_pin10), .pin9(inv_restart_cycle));  // open: pin7
  not not_1 (reset_sync, n74138_1_pin15);
  not not_2 (reset_low_cycle, n74138_1_pin14);
  not not_3 (reset_high_cycle, n74138_1_pin13);
  not not_4 (fetch_cycle, n74138_1_pin12);
  not not_5 (low_cycle, n74138_1_pin11);
  not not_6 (high_cycle, n74138_1_pin10);
  // also tied to GND on the sheet: {n74193_1_pin10, n74138_1_pin4}
  // also tied to VCC on the sheet: {n74193_1_pin4, n74193_1_pin1, n74193_1_pin15}

  // Notes on the sheet:
  //   inv_CLOCK: initial=0x1
  //   inv_UC_restart_cycle: initial=0x1
  //   inv_UC_halt: initial=0x1
endmodule

module decodificador (
  input  inv_UC_clear_interrupt_mask,
  input  INT_REQUEST,
  input  inv_UC_set_interrupt_mask,
  input  [7:0] DATA,
  input  reset_sync,
  input  inv_UC_restart_cycle,
  input  reset_low_cycle,
  input  reset_high_cycle,
  input  inv_UC_int_ready,
  input  fetch_clock,
  input  fetch_cycle,
  input  low_cycle,
  input  high_cycle,
  output [9:0] select_opcode,
  output [7:0] INS,
  output INT_MASK_FLAG
);

  wire and_1_out, int_pending, n7474_1_pin2, n7474_1_pin4, n7474_1_pin11, n7474_1_pin12, n7474_2_pin10,
       n7474_2_pin11, n74138_1_pin7, n74138_1_pin9, n74138_1_pin10, n74138_1_pin11, n74138_1_pin12,
       n74138_1_pin13, n74138_1_pin14, n74138_1_pin15, n74157_1_pin15, n74157_2_pin15, n74377_1_pin1,
       or_1_out, Q0, Q1, Q2, Q3, Q4, Q5, Q6, Q7;

  _74377 u_74377_1 (
    .pin1(n74377_1_pin1), .pin2(Q0), .pin3(DATA[0]), .pin4(DATA[1]), .pin5(Q1), .pin6(Q2), .pin7(DATA[2]),
    .pin8(DATA[3]), .pin9(Q3), .pin19(Q7), .pin18(DATA[7]), .pin17(DATA[6]), .pin16(Q6), .pin15(Q5),
    .pin14(DATA[5]), .pin13(DATA[4]), .pin12(Q4), .pin11(fetch_clock));
  _74157 u_74157_1 (
    .pin1(fetch_cycle), .pin2(Q0), .pin3(DATA[0]), .pin4(INS[0]), .pin5(Q1), .pin6(DATA[1]), .pin7(INS[1]),
    .pin15(n74157_1_pin15), .pin14(Q3), .pin13(DATA[3]), .pin12(INS[3]), .pin11(Q2), .pin10(DATA[2]),
    .pin9(INS[2]));
  or or_1 (or_1_out, fetch_cycle, low_cycle, high_cycle);
  _74157 u_74157_2 (
    .pin1(fetch_cycle), .pin2(Q4), .pin3(DATA[4]), .pin4(INS[4]), .pin5(Q5), .pin6(DATA[5]), .pin7(INS[5]),
    .pin15(n74157_2_pin15), .pin14(Q7), .pin13(DATA[7]), .pin12(INS[7]), .pin11(Q6), .pin10(DATA[6]),
    .pin9(INS[6]));
  _74138 u_74138_1 (
    .pin1(INS[5]), .pin2(INS[6]), .pin3(INS[7]), .pin4(select_opcode[8]), .pin5(select_opcode[8]),
    .pin6(or_1_out), .pin7(n74138_1_pin7), .pin15(n74138_1_pin15), .pin14(n74138_1_pin14),
    .pin13(n74138_1_pin13), .pin12(n74138_1_pin12), .pin11(n74138_1_pin11), .pin10(n74138_1_pin10),
    .pin9(n74138_1_pin9));
  not not_1 (select_opcode[0], n74138_1_pin15);
  not not_2 (select_opcode[1], n74138_1_pin14);
  not not_3 (select_opcode[2], n74138_1_pin13);
  not not_4 (select_opcode[3], n74138_1_pin12);
  not not_5 (select_opcode[4], n74138_1_pin11);
  not not_6 (select_opcode[5], n74138_1_pin10);
  not not_7 (select_opcode[6], n74138_1_pin9);
  not not_8 (select_opcode[7], n74138_1_pin7);
  or or_2 (select_opcode[9], reset_sync, reset_low_cycle, reset_high_cycle);
  and and_1 (and_1_out, INT_REQUEST, INT_MASK_FLAG);
  _7474 u_7474_1 (
    .pin1(inv_UC_int_ready), .pin2(n7474_1_pin2), .pin3(and_1_out), .pin4(n7474_1_pin4), .pin5(int_pending),
    .pin13(inv_UC_clear_interrupt_mask), .pin12(n7474_1_pin12), .pin11(n7474_1_pin11),
    .pin10(inv_UC_set_interrupt_mask), .pin9(INT_MASK_FLAG));  // open: pin6, pin8
  _7474 u_7474_2 (
    .pin13(inv_UC_restart_cycle), .pin12(int_pending), .pin11(n7474_2_pin11), .pin10(n7474_2_pin10),
    .pin9(select_opcode[8]));  // open: pin1, pin2, pin3, pin4, pin5, pin6, pin8
  not not_9 (n7474_2_pin11, inv_UC_int_ready);
  // also tied to GND on the sheet: {n74377_1_pin1, n74157_1_pin15, n74157_2_pin15, n7474_1_pin12, n7474_1_pin11}
  // also tied to VCC on the sheet: {n7474_1_pin2, n7474_1_pin4, n7474_2_pin10}

  // Other names for the same wires on the sheet: select_opcode_int = select_opcode[8]

  // Notes on the sheet:
  //   inv_UC_restart_cycle: initial=0x1
  //   inv_UC_set_interrupt_mask: initial=0x1
  //   inv_UC_clear_interrupt_mask: initial=0x1
endmodule
